// Logisim project alu.circ as structural Verilog: 1 circuit, main circuit main
module main (
  input  [31:0] X,
  input  [31:0] Y,
  input  [5:0] Switch__S,
  output Signed_Overflow,
  output [31:0] RESULT,
  output Equal
);

  wire [4:0] bit_extender_1_out;
  wire [31:0] adder_1_out, adder_2_out, and_1_out, comparator_1_lt, comparator_2_lt, comparator_3_eq,
       or_1_out, shifter_1_out, shifter_2_out, shifter_3_out, shifter_4_out, subtractor_1_out,
       subtractor_2_out;

  Bit_Extender #(.in_width(32), .out_width(5)) bit_extender_1 (.in(Y), .out(bit_extender_1_out));
  Shifter #(.width(32)) shifter_1 (.in(X), .\dist (bit_extender_1_out), .out(shifter_1_out));
  Shifter #(.width(32), .shift("lr")) shifter_2 (.in(X), .\dist (bit_extender_1_out), .out(shifter_2_out));
  Shifter #(.width(32), .shift("ar")) shifter_3 (.in(X), .\dist (bit_extender_1_out), .out(shifter_3_out));
  Adder #(.width(32)) adder_1 (.a(X), .b(Y), .out(adder_1_out));  // open: cin, cout
  Adder #(.width(32)) adder_2 (.a(X), .b(Y), .out(adder_2_out));  // open: cin, cout
  Subtractor #(.width(32)) subtractor_1 (.a(X), .b(Y), .out(subtractor_1_out));  // open: bin, bout
  Subtractor #(.width(32)) subtractor_2 (.a(X), .b(Y), .out(subtractor_2_out));  // open: bin, bout
  assign and_1_out = X & Y;  // AND_Gate and_1, 32 bits wide
  assign or_1_out = X | Y;  // OR_Gate or_1, 32 bits wide
  Comparator #(.width(32)) comparator_1 (.a(X), .b(Y), .lt(comparator_1_lt[0]));  // open: gt, eq
  Comparator #(.width(32)) comparator_2 (.a(X), .b(Y), .lt(comparator_2_lt[0]));  // open: gt, eq
  Comparator #(.width(32)) comparator_3 (.a(X), .b(Y), .eq(comparator_3_eq[0]));  // open: gt, lt
  Shifter #(.width(32)) shifter_4 (.in(X), .\dist (bit_extender_1_out), .out(shifter_4_out));
  Multiplexer #(.select(5), .width(32), .enable("false")) multiplexer_1 (
    .in0(shifter_1_out), .in2(shifter_2_out), .in3(shifter_3_out), .in16(adder_1_out), .in17(adder_2_out),
    .in18(subtractor_1_out), .in19(subtractor_2_out), .in20(and_1_out), .in21(or_1_out),
    .in26(comparator_1_lt), .in27(comparator_2_lt), .in30(comparator_3_eq), .in31(shifter_4_out),
    .out(RESULT), .sel({Switch__S[5], Switch__S[3:0]}));  // open: in1, in4, in5, in6, in7, in8, in9, in10, in11, in12, in13, in14, in15, in22, in23, in24, in25, in28, in29
  // Pins of 1 and 32 bits meet at comparator_2_lt
  // Pins of 1 and 32 bits meet at comparator_1_lt
  // Pins of 1 and 32 bits meet at comparator_3_eq

  // Notes on the sheet:
  //   INPUTS to your circuit
  //   INPUT to your circuit
  //   DON'T CHANGE THE INPUTS AND OUTPUTS! IF YOU DO SO, YOU NEED TO MAKE SURE THE PINS ARE IN THE RIGHT PLACES!
  //   OUTPUTS of your circuit
endmodule
