// Logisim project cpu.circ as structural Verilog: 3 circuits, main circuit main
module main (
  input  [31:0] RS_READ_VALUE,
  input  [31:0] RT_READ_VALUE,
  input  [31:0] INSTRUCTION,
  input  [5:0] jump_op,
  input  CLOCK,
  input  RESET,
  output [31:0] t0,
  output [31:0] t1,
  output [31:0] t2,
  output [31:0] t3,
  output [4:0] RS,
  output [4:0] RT,
  output [4:0] Write_Register,
  output [31:0] RD_WRITE_VALUE,
  output RD_WRITE_ENABLE,
  output [23:0] FETCH_ADDRESS
);

  wire ALU_equal, ALU_signed_overflow, comparator_1_eq, reg_select_1_rs__tx, reg_select_1_rt__tx;
  wire [1:0] rs_to_regfile, rt_to_regfile;
  wire [2:0] inst_select_1_inst_selector;
  wire [4:0] RD, RS_t, RT_t, SHAMT;
  wire [4:2] demultiplexer_2_out1, demultiplexer_3_out1;
  wire [5:0] FUNCT, multiplexer_2_out, OP;
  wire [15:0] ADDR_IMM;
  wire [25:0] ADDR;
  wire [31:0] bit_extender_1_out, multiplexer_1_out;

  Demultiplexer #(.select(3), .width(32), .enable("false")) demultiplexer_1 (
    .out1({OP, ADDR}), .out2({OP, RS_t, RT_t, ADDR_IMM}), .out5({OP, RS_t, RT_t, RD, SHAMT, FUNCT}),
    .in(INSTRUCTION), .sel(inst_select_1_inst_selector));  // open: out0, out3, out4, out6, out7
  inst_select inst_select_1 (.INSTRUCTION(INSTRUCTION), .jump_op(jump_op), .Inst_selector(inst_select_1_inst_selector));
  Comparator #(.width(6)) comparator_1 (.a(OP), .b({6{1'b0}}), .eq(comparator_1_eq));  // open: gt, lt
  Multiplexer #(.width(32), .enable("false")) multiplexer_1 (
    .in0(RT_READ_VALUE), .in1(bit_extender_1_out), .out(multiplexer_1_out), .sel(comparator_1_eq));
  Multiplexer #(.width(6), .enable("false")) multiplexer_2 (
    .in0(OP), .in1(FUNCT), .out(multiplexer_2_out), .sel(comparator_1_eq));
  alu_main ALU (
    .Switch__S(multiplexer_2_out), .X(RS_READ_VALUE), .Equal(ALU_equal), .RESULT(RD_WRITE_VALUE),
    .Signed_Overflow(ALU_signed_overflow), .Y(multiplexer_1_out));
  Demultiplexer #(.width(5), .enable("false")) demultiplexer_2 (
    .out0(RS), .out1({demultiplexer_2_out1, rs_to_regfile}), .in(RS_t), .sel(reg_select_1_rs__tx));
  reg_select reg_select_1 (.RS(RS_t), .RT(RT_t), .RS__tx(reg_select_1_rs__tx), .RT__tx(reg_select_1_rt__tx));
  Demultiplexer #(.width(5), .enable("false")) demultiplexer_3 (
    .out0(RT), .out1({demultiplexer_3_out1, rt_to_regfile}), .in(RT_t), .sel(reg_select_1_rt__tx));
  assign bit_extender_1_out = {{16{ADDR_IMM[15]}}, ADDR_IMM};  // Bit_Extender bit_extender_1
  LED led_1 (.in(ALU_signed_overflow));
  // mem_main MEM: pin names not known
  regfile_main RegFile (
    .write_register(Write_Register[1:0]), .write_data(RD_WRITE_VALUE), .Read_Data_1(RS_READ_VALUE),
    .Read_Data_2(RT_READ_VALUE), .t0_Value(t0), .t1_Value(t1), .t2_Value(t2), .t3_Value(t3),
    .Read_register_1(rs_to_regfile), .Read_register_2(rt_to_regfile), .RegWrite(RD_WRITE_ENABLE),
    .clock(CLOCK));

  // Other names for the same wires on the sheet: rs_to_run[4:0] = RS; rt_to_run[4:0] = RT

  // Notes on the sheet:
  //   These are outputs/inputs from run.circ
  //   alu_src
  //   alu_ctr
  //   branch_logic
  //   These are outputs to run.circ
endmodule

module reg_select (
  input  [4:0] RS,
  input  [4:0] RT,
  output RS__tx,
  output RT__tx
);

  wire comparator_1_lt, comparator_2_lt, comparator_3_gt, comparator_4_gt;

  Comparator #(.width(5)) comparator_1 (.a(RS), .b(5'b01100), .lt(comparator_1_lt));  // open: gt, eq
  Comparator #(.width(5)) comparator_2 (.a(RT), .b(5'b01100), .lt(comparator_2_lt));  // open: gt, eq
  Comparator #(.width(5)) comparator_3 (.a(RS), .b(5'b00111), .gt(comparator_3_gt));  // open: eq, lt
  Comparator #(.width(5)) comparator_4 (.a(RT), .b(5'b00111), .gt(comparator_4_gt));  // open: eq, lt
  and and_1 (RS__tx, comparator_3_gt, comparator_1_lt);
  and and_2 (RT__tx, comparator_4_gt, comparator_2_lt);
endmodule

module inst_select (
  input  [31:0] INSTRUCTION,
  input  [5:0] jump_op,
  output [2:0] Inst_selector
);

  // Probe on INSTRUCTION
  Comparator #(.width(6)) comparator_1 (.a({6{1'b0}}), .b(INSTRUCTION[31:26]), .eq(Inst_selector[2]));  // open: gt, lt
  Comparator #(.width(6)) comparator_2 (
    .a(INSTRUCTION[31:26]), .b(jump_op), .gt(Inst_selector[1]), .eq(Inst_selector[0]));  // open: lt
endmodule
